# Fritzing sketch ExoProg (saved by Fritzing 0.8.7b)
circuit board: 6.87603cm x 6.49802cm
breadboards: 1

parts:
  C1 = Ceramic Capacitor [capacitance="100 nF" package="0603 [SMD, multilayer]"]
  R1 = Resistor [tolerance=±5% resistance=10k package=THT]
  U2 = 74HC4052 [part_number=74HC4052 package=dil16]
  C2 = Ceramic Capacitor [capacitance="100 nF" package="0603 [SMD, multilayer]"]
  C3 = Ceramic Capacitor [capacitance="100 nF" package="0603 [SMD, multilayer]"]
  U3 = 74HC4052 [part_number=74HC4052 package=dil16]
  IC1 = IC, DIP package, 8 pins [chip_label=Kabel]
  IC2 = IC, DIP package, 8 pins [chip_label=ATtiny]
  J5 = shrouded pin header, 6 pins [form="♂ (shrouded male)"]

nets:
  5V: C1.0, R1.Pin_1, U2.VCC, C2.0, C3.0, U3.VCC, IC2.pin8, J5.pin6
  GND: C1.1, U2.INH, U2.VEE, U2.GND, U2.B, C2.1, C3.1, U3.INH, U3.VEE, U3.GND, U3.B, IC1.pin4, IC2.pin4, J5.pin4
  N1: R1.Pin_0, U3.Y, IC2.pin1
  N2: U2.Y0, J5.pin5
  N3: U2.Y, IC2.pin7
  N4: U2.Y1, IC1.pin7
  N5: U2.A, U3.Y0, U3.A, J5.pin3
  N6: U2.X0, J5.pin2
  N7: U2.X, IC2.pin5
  N8: U2.X1, IC1.pin5
  N9: U3.Y1, IC1.pin1
  N10: U3.X0, J5.pin1
  N11: U3.X, IC2.pin6
  N12: U3.X1, IC1.pin6
  N13: IC1.pin2, IC2.pin2
  N14: IC1.pin3, IC2.pin3
